// Logisim project btc_miner.circ as structural Verilog: 1 circuit, main circuit main
module main (
  input  [31:0] w_15,
  input  [31:0] g,
  input  [31:0] f,
  input  [31:0] w_2,
  input  [31:0] e,
  output [15:0] pc,
  output [6:0] out_7,
  output [31:0] t_2,
  output [31:0] out_9,
  output [31:0] out_10,
  output [31:0] t_7,
  output [31:0] t_15,
  output [31:0] out_13,
  output [31:0] t_16,
  output [31:0] out_15,
  output [3:0] number_of_digit_counter,
  output [5:0] out_17,
  output [5:0] out_18,
  output [5:0] out_19,
  output [5:0] out_20,
  output [31:0] rotate_7,
  output [31:0] right_3,
  output [31:0] rotate_18,
  output [5:0] out_24,
  output [5:0] out_25,
  output [31:0] small_sigma_0,
  output [31:0] sigma_1,
  output [5:0] out_28,
  output [5:0] out_29,
  output [31:0] ch,
  output [31:0] small_sigma_1,
  output [31:0] out_32,
  output [31:0] out_33,
  output [31:0] out_34,
  output [31:0] out_35,
  output [31:0] out_36,
  output [31:0] out_37,
  output [31:0] sigma_0,
  output [31:0] out_39,
  output [31:0] out_40
);

  wire and_1_out, and_2_out, buffer_1_out, buffer_2_out, buffer_3_out, buffer_4_out, buffer_5_out,
       buffer_6_out, clock_1_out, comparator_1_gt, d_ff_1_q, d_ff_2_q, d_ff_3_q, d_ff_4_q, d_ff_5_q,
       d_ff_6_q, d_ff_7_q, d_ff_8_q, d_ff_9_q, d_ff_10_q, d_ff_11_q, d_ff_12_q, demultiplexer_1_out1,
       demultiplexer_1_out2, demultiplexer_1_out3, demultiplexer_1_out4, demultiplexer_1_out5,
       demultiplexer_1_out6, demultiplexer_1_out7, demultiplexer_1_out8, demultiplexer_1_out9,
       demultiplexer_1_out10, demultiplexer_1_out11, demultiplexer_1_out12, keyboard_1_avail, not_1_out,
       t_ff_1_qn, t_ff_2_qn, t_ff_3_qn, t_ff_4_qn, t_ff_5_qn, t_ff_6_qn, t_ff_8_qn, t_ff_9_qn, t_ff_10_qn,
       t_ff_11_qn, t_ff_12_qn, t_ff_13_qn, t_ff_14_qn, t_ff_15_qn, t_ff_16_qn, t_ff_17_qn, t_ff_18_qn,
       t_ff_19_qn, t_ff_21_qn, t_ff_22_qn, t_ff_23_qn, t_ff_24_qn, t_ff_25_qn, t_ff_26_qn, undriven,
       undriven_13, undriven_30, undriven_33;
  wire [2:0] undriven_15, undriven_16, undriven_23;
  wire [5:0] bit_extender_4_out, bit_extender_5_out, bit_extender_6_out, bit_extender_7_out, not_3_out,
       not_4_out, not_5_out, not_6_out, t_ff_21_q;
  wire [5:5] subtractor_1_bout, subtractor_2_bout, subtractor_3_bout, subtractor_4_bout;
  wire [7:0] bit_extender_1_out, pull_resistor_1_node, register_1_q, register_2_q, register_3_q,
       register_4_q, register_5_q, register_6_q, register_7_q, register_8_q, register_9_q, register_10_q,
       register_11_q, register_12_q, register_13_q, register_14_q, register_17_q;
  wire [15:0] bit_extender_2_out;
  wire [31:0] and_3_out, and_4_out, bit_extender_3_out, multiplexer_9_out, multiplexer_13_out,
       multiplexer_14_out, multiplexer_15_out, multiplexer_16_out, multiplexer_25_out, multiplexer_29_out,
       multiplexer_30_out, multiplexer_31_out, multiplexer_32_out, not_2_out, register_18_q, register_19_q,
       register_20_q, register_21_q, register_22_q, register_23_q, register_24_q, register_25_q,
       register_26_q, register_27_q, register_28_q, register_29_q, register_30_q, register_31_q,
       register_32_q, register_33_q, register_34_q, register_35_q, register_36_q, register_37_q,
       register_38_q, register_39_q, register_40_q, register_41_q, register_42_q, register_43_q,
       register_44_q, register_45_q, register_46_q, register_47_q, register_48_q, register_49_q,
       register_50_q, register_51_q, register_52_q, register_53_q, register_54_q, register_55_q,
       register_56_q, register_57_q, register_58_q, register_59_q, register_60_q, register_61_q,
       register_62_q, register_63_q, register_64_q, register_65_q, register_66_q, register_67_q,
       register_68_q, register_69_q, register_70_q, register_71_q, register_72_q, register_73_q,
       register_74_q, register_75_q, register_76_q, register_77_q, register_78_q, register_79_q,
       register_80_q, register_81_q, register_82_q, register_83_q, undriven_2, undriven_3, undriven_4,
       undriven_5, undriven_6, undriven_7, undriven_8, undriven_9, undriven_10, undriven_11, undriven_12,
       undriven_14, undriven_17, undriven_18, undriven_19, undriven_20, undriven_21, undriven_22,
       undriven_24, undriven_25, undriven_26, undriven_27, undriven_28, undriven_29, undriven_31,
       undriven_32, undriven_34, w0_q, w1_q, xor_1_out, xor_2_out, xor_4_out, xor_7_out;

  Clock clock_1 (.out(clock_1_out));
  T_Flip_Flop t_ff_1 (
    .T(1'b1), .clk(buffer_2_out), .Q(number_of_digit_counter[0]), .Qn(t_ff_1_qn));  // open: reset, preset
  T_Flip_Flop t_ff_2 (.T(1'b1), .clk(clock_1_out), .Q(pc[0]), .Qn(t_ff_2_qn));  // open: reset, preset
  Demultiplexer #(.select(4)) demultiplexer_1 (
    .out1(demultiplexer_1_out1), .out2(demultiplexer_1_out2), .out3(demultiplexer_1_out3),
    .out4(demultiplexer_1_out4), .out5(demultiplexer_1_out5), .out6(demultiplexer_1_out6),
    .out7(demultiplexer_1_out7), .out8(demultiplexer_1_out8), .out9(demultiplexer_1_out9),
    .out10(demultiplexer_1_out10), .out11(demultiplexer_1_out11), .out12(demultiplexer_1_out12), .in(1'b1),
    .sel(number_of_digit_counter));  // open: out0, out13, out14, out15
  T_Flip_Flop t_ff_3 (
    .T(1'b1), .clk(t_ff_1_qn), .Q(number_of_digit_counter[1]), .Qn(t_ff_3_qn));  // open: reset, preset
  T_Flip_Flop t_ff_4 (.T(1'b1), .clk(t_ff_2_qn), .Q(pc[1]), .Qn(t_ff_4_qn));  // open: reset, preset
  Keyboard keyboard_1 (.clk(clock_1_out), .avail(keyboard_1_avail), .data(out_7));  // open: re, clr
  T_Flip_Flop t_ff_5 (
    .T(1'b1), .clk(t_ff_3_qn), .Q(number_of_digit_counter[2]), .Qn(t_ff_5_qn));  // open: reset, preset
  T_Flip_Flop t_ff_6 (.T(1'b1), .clk(t_ff_4_qn), .Q(pc[2]), .Qn(t_ff_6_qn));  // open: reset, preset
  D_Flip_Flop d_ff_1 (.D(demultiplexer_1_out9), .clk(clock_1_out), .Q(d_ff_1_q));  // open: Qn, preset, reset
  D_Flip_Flop d_ff_2 (.D(demultiplexer_1_out10), .clk(clock_1_out), .Q(d_ff_2_q));  // open: Qn, preset, reset
  D_Flip_Flop d_ff_3 (.D(demultiplexer_1_out11), .clk(clock_1_out), .Q(d_ff_3_q));  // open: Qn, preset, reset
  D_Flip_Flop d_ff_4 (.D(demultiplexer_1_out12), .clk(clock_1_out), .Q(d_ff_4_q));  // open: Qn, preset, reset
  T_Flip_Flop t_ff_7 (.T(1'b1), .clk(t_ff_5_qn), .Q(number_of_digit_counter[3]));  // open: Qn, reset, preset
  T_Flip_Flop t_ff_8 (.T(1'b1), .clk(t_ff_6_qn), .Q(pc[3]), .Qn(t_ff_8_qn));  // open: reset, preset
  and and_1 (and_1_out, keyboard_1_avail, clock_1_out);
  T_Flip_Flop t_ff_9 (.T(1'b1), .clk(t_ff_8_qn), .Q(pc[4]), .Qn(t_ff_9_qn));  // open: reset, preset
  assign bit_extender_1_out = {{1{1'b0}}, out_7};  // Bit_Extender bit_extender_1
  buf buffer_1 (buffer_1_out, and_1_out);
  T_Flip_Flop t_ff_10 (.T(1'b1), .clk(t_ff_9_qn), .Q(pc[5]), .Qn(t_ff_10_qn));  // open: reset, preset
  Register register_1 (.D(bit_extender_1_out), .clk(and_1_out), .Q(register_1_q));  // open: en, clr
  buf buffer_2 (buffer_2_out, buffer_1_out);
  D_Flip_Flop d_ff_5 (.D(demultiplexer_1_out1), .clk(clock_1_out), .Q(d_ff_5_q));  // open: Qn, preset, reset
  D_Flip_Flop d_ff_6 (.D(demultiplexer_1_out2), .clk(clock_1_out), .Q(d_ff_6_q));  // open: Qn, preset, reset
  D_Flip_Flop d_ff_7 (.D(demultiplexer_1_out3), .clk(clock_1_out), .Q(d_ff_7_q));  // open: Qn, preset, reset
  D_Flip_Flop d_ff_8 (.D(demultiplexer_1_out4), .clk(clock_1_out), .Q(d_ff_8_q));  // open: Qn, preset, reset
  D_Flip_Flop d_ff_9 (.D(demultiplexer_1_out5), .clk(clock_1_out), .Q(d_ff_9_q));  // open: Qn, preset, reset
  D_Flip_Flop d_ff_10 (.D(demultiplexer_1_out6), .clk(clock_1_out), .Q(d_ff_10_q));  // open: Qn, preset, reset
  D_Flip_Flop d_ff_11 (.D(demultiplexer_1_out7), .clk(clock_1_out), .Q(d_ff_11_q));  // open: Qn, preset, reset
  D_Flip_Flop d_ff_12 (.D(demultiplexer_1_out8), .clk(clock_1_out), .Q(d_ff_12_q));  // open: Qn, preset, reset
  T_Flip_Flop t_ff_11 (.T(1'b1), .clk(t_ff_10_qn), .Q(pc[6]), .Qn(t_ff_11_qn));  // open: reset, preset
  T_Flip_Flop t_ff_12 (.T(1'b1), .clk(t_ff_11_qn), .Q(pc[7]), .Qn(t_ff_12_qn));  // open: reset, preset
  T_Flip_Flop t_ff_13 (.T(1'b1), .clk(t_ff_12_qn), .Q(pc[8]), .Qn(t_ff_13_qn));  // open: reset, preset
  Register register_2 (.D(register_1_q), .clk(d_ff_5_q), .Q(register_2_q));  // open: en, clr
  Register register_3 (.D(register_1_q), .clk(d_ff_6_q), .Q(register_3_q));  // open: en, clr
  Register register_4 (.D(register_1_q), .clk(d_ff_7_q), .Q(register_4_q));  // open: en, clr
  Register register_5 (.D(register_1_q), .clk(d_ff_8_q), .Q(register_5_q));  // open: en, clr
  Register register_6 (.D(register_1_q), .clk(d_ff_9_q), .Q(register_6_q));  // open: en, clr
  Register register_7 (.D(register_1_q), .clk(d_ff_10_q), .Q(register_7_q));  // open: en, clr
  Register register_8 (.D(register_1_q), .clk(d_ff_11_q), .Q(register_8_q));  // open: en, clr
  Register register_9 (.D(register_1_q), .clk(d_ff_12_q), .Q(register_9_q));  // open: en, clr
  T_Flip_Flop t_ff_14 (.T(1'b1), .clk(t_ff_13_qn), .Q(pc[9]), .Qn(t_ff_14_qn));  // open: reset, preset
  T_Flip_Flop t_ff_15 (.T(1'b1), .clk(t_ff_14_qn), .Q(pc[10]), .Qn(t_ff_15_qn));  // open: reset, preset
  T_Flip_Flop t_ff_16 (.T(1'b1), .clk(t_ff_15_qn), .Q(pc[11]), .Qn(t_ff_16_qn));  // open: reset, preset
  T_Flip_Flop t_ff_17 (.T(1'b1), .clk(t_ff_16_qn), .Q(pc[12]), .Qn(t_ff_17_qn));  // open: reset, preset
  Pull_Resistor pull_resistor_1 (.node(pull_resistor_1_node));
  T_Flip_Flop t_ff_18 (.T(1'b1), .clk(t_ff_17_qn), .Q(pc[13]), .Qn(t_ff_18_qn));  // open: reset, preset
  Register register_10 (.D(register_1_q), .clk(d_ff_1_q), .Q(register_10_q));  // open: en, clr
  Register register_11 (.D(register_1_q), .clk(d_ff_2_q), .Q(register_11_q));  // open: en, clr
  Register register_12 (.D(register_1_q), .clk(d_ff_3_q), .Q(register_12_q));  // open: en, clr
  Register register_13 (.D(register_1_q), .clk(d_ff_4_q), .Q(register_13_q));  // open: en, clr
  Register register_14 (.D(8'h80), .clk(buffer_2_out), .Q(register_14_q));  // open: en, clr
  Register register_15 (.D(pull_resistor_1_node), .clk(buffer_2_out));  // open: en, Q, clr
  Register register_16 (.D(pull_resistor_1_node), .clk(buffer_2_out));  // open: en, Q, clr
  Register register_17 (.D(8'hc0), .clk(buffer_2_out), .Q(register_17_q));  // open: en, clr
  and and_2 (and_2_out, clock_1_out, not_1_out);
  assign bit_extender_2_out = {{12{1'b0}}, 4'b0011};  // Bit_Extender bit_extender_2
  T_Flip_Flop t_ff_19 (.T(1'b1), .clk(t_ff_18_qn), .Q(pc[14]), .Qn(t_ff_19_qn), .preset(undriven));  // open: reset
  T_Flip_Flop t_ff_20 (.T(1'b1), .clk(t_ff_19_qn), .Q(pc[15]));  // open: Qn, reset, preset
  Comparator #(.width(16)) comparator_1 (.a(bit_extender_2_out), .b(pc), .gt(comparator_1_gt));  // open: eq, lt
  not not_1 (not_1_out, comparator_1_gt);
  Register #(.width(32)) w0 (
    .D({register_5_q, register_4_q, register_3_q, register_2_q}), .clk(and_2_out), .Q(w0_q));  // open: en, clr
  Register #(.width(32)) w1 (
    .D({register_9_q, register_8_q, register_7_q, register_6_q}), .clk(and_2_out), .Q(w1_q));  // open: en, clr
  assign bit_extender_3_out = {{24{1'b0}}, register_17_q};  // Bit_Extender bit_extender_3
  assign xor_1_out = {undriven_2[19], undriven_2[20], undriven_2[18:0], undriven_2[31:21]} ^ undriven_2;  // XOR_Gate xor_1, 32 bits wide
  assign xor_2_out = {w_15[17:0], w_15[31:18]} ^ {w_15[6:0], w_15[31:7]};  // XOR_Gate xor_2, 32 bits wide
  assign sigma_0 = xor_1_out ^ {undriven_2[8:0], undriven_2[31:9]};  // XOR_Gate xor_3, 32 bits wide
  assign xor_4_out = {w_2[16:0], w_2[31:17]} ^ {w_2[18:0], w_2[31:19]};  // XOR_Gate xor_4, 32 bits wide
  Register #(.width(32)) register_18 (
    .D({register_13_q, register_12_q, register_11_q, register_10_q}), .clk(and_2_out), .Q(register_18_q));  // open: en, clr
  assign small_sigma_0 = xor_2_out ^ {3'b000, w_15[31:3]};  // XOR_Gate xor_5, 32 bits wide
  assign small_sigma_1 = xor_4_out ^ {{10{1'b0}}, w_2[31:10]};  // XOR_Gate xor_6, 32 bits wide
  Register #(.width(32)) register_19 (
    .D({{24{1'b0}}, register_14_q}), .clk(and_2_out), .Q(register_19_q));  // open: en, clr
  buf buffer_3 (buffer_3_out, and_2_out);
  buf buffer_4 (buffer_4_out, buffer_3_out);
  ROM #(.addrWidth(3), .dataWidth(32)) h_values ();  // open: addr, data
  ROM #(.addrWidth(6), .dataWidth(32)) k_values ();  // open: addr, data
  Register #(.width(32)) register_20 (.D(undriven_3), .clk(undriven_13), .Q(register_20_q));  // open: en, clr
  Register #(.width(32)) register_21 (.D(undriven_4), .clk(undriven_13), .Q(register_21_q));  // open: en, clr
  Register #(.width(32)) register_22 (.clk(undriven_13), .Q(register_22_q));  // open: D, en, clr
  Register #(.width(32)) register_23 (.clk(undriven_13), .Q(register_23_q));  // open: D, en, clr
  Register #(.width(32)) register_24 (.D(undriven_7), .clk(undriven_13), .Q(register_24_q));  // open: en, clr
  Register #(.width(32)) register_25 (.D(undriven_6), .clk(undriven_13), .Q(register_25_q));  // open: en, clr
  Register #(.width(32)) register_26 (.D(undriven_5), .clk(undriven_13), .Q(register_26_q));  // open: en, clr
  Register #(.width(32)) register_27 (.D(undriven_5), .clk(undriven_13), .Q(register_27_q));  // open: en, clr
  assign not_2_out = ~e;  // NOT_Gate not_2, 32 bits wide
  Multiplexer #(.select(3), .width(32)) multiplexer_1 (
    .in0(register_20_q), .in1(register_21_q), .in2(register_22_q), .in3(register_23_q), .in4(register_24_q),
    .in5(register_25_q), .in6(register_26_q), .in7(register_27_q), .out(out_32), .sel(out_17[2:0]));
  Register #(.width(32)) register_28 (.D(w0_q), .clk(buffer_4_out), .Q(register_28_q));  // open: en, clr
  Register #(.width(32)) register_29 (.D(w1_q), .clk(buffer_4_out), .Q(register_29_q));  // open: en, clr
  Register #(.width(32)) register_30 (.D(register_18_q), .clk(buffer_4_out), .Q(register_30_q));  // open: en, clr
  Register #(.width(32)) register_31 (.D(register_19_q), .clk(buffer_4_out), .Q(register_31_q));  // open: en, clr
  Register #(.width(32)) register_32 (.D(undriven_10), .clk(buffer_4_out), .Q(register_32_q));  // open: en, clr
  Register #(.width(32)) register_33 (.D(undriven_9), .clk(buffer_4_out), .Q(register_33_q));  // open: en, clr
  Register #(.width(32)) register_34 (.D(undriven_8), .clk(buffer_4_out), .Q(register_34_q));  // open: en, clr
  Register #(.width(32)) register_35 (.D(undriven_8), .clk(buffer_4_out), .Q(register_35_q));  // open: en, clr
  assign and_3_out = f & e;  // AND_Gate and_3, 32 bits wide
  assign and_4_out = g & not_2_out;  // AND_Gate and_4, 32 bits wide
  Multiplexer #(.select(3), .width(32)) multiplexer_2 (
    .in0(register_20_q), .in1(register_21_q), .in2(register_22_q), .in3(register_23_q), .in4(register_24_q),
    .in5(register_25_q), .in6(register_26_q), .in7(register_27_q), .out(out_34), .sel(out_19[2:0]));
  Multiplexer #(.select(3), .width(32)) multiplexer_3 (
    .in0(register_20_q), .in1(register_21_q), .in2(register_22_q), .in3(register_23_q), .in4(register_24_q),
    .in5(register_25_q), .in6(register_26_q), .in7(register_27_q), .out(out_36), .sel(out_24[2:0]));
  assign ch = and_3_out | and_4_out;  // OR_Gate or_1, 32 bits wide
  Multiplexer #(.select(3), .width(32)) multiplexer_4 (
    .in0(register_20_q), .in1(register_21_q), .in2(register_22_q), .in3(register_23_q), .in4(register_24_q),
    .in5(register_25_q), .in6(register_26_q), .in7(register_27_q), .out(out_39), .sel(out_28[2:0]));
  T_Flip_Flop t_ff_21 (.T(1'b1), .clk(buffer_6_out), .Q(t_ff_21_q[0]), .Qn(t_ff_21_qn));  // open: reset, preset
  assign xor_7_out = {undriven_12[0], undriven_12[1], undriven_12[2], undriven_12[3], undriven_12[4], undriven_12[5], undriven_12[31:6]} ^ {undriven_12[10:0], undriven_12[31:11]};  // XOR_Gate xor_7, 32 bits wide
  Register #(.width(32)) register_36 (.D(undriven_14), .clk(undriven_13), .Q(register_36_q));  // open: en, clr
  Register #(.width(32)) register_37 (.D(undriven_7), .clk(undriven_13), .Q(register_37_q));  // open: en, clr
  Register #(.width(32)) register_38 (.D(undriven_7), .clk(undriven_13), .Q(register_38_q));  // open: en, clr
  Register #(.width(32)) register_39 (.D(undriven_7), .clk(undriven_13), .Q(register_39_q));  // open: en, clr
  Register #(.width(32)) register_40 (.D(undriven_7), .clk(undriven_13), .Q(register_40_q));  // open: en, clr
  Register #(.width(32)) register_41 (.D(undriven_7), .clk(undriven_13), .Q(register_41_q));  // open: en, clr
  Register #(.width(32)) register_42 (.D(undriven_7), .clk(undriven_13), .Q(register_42_q));  // open: en, clr
  Register #(.width(32)) register_43 (.D(undriven_11), .clk(undriven_13), .Q(register_43_q));  // open: en, clr
  Multiplexer #(.select(3), .width(32)) multiplexer_5 (
    .in0(register_28_q), .in1(register_29_q), .in2(register_30_q), .in3(register_31_q), .in4(register_32_q),
    .in5(register_33_q), .in6(register_34_q), .in7(register_35_q), .out(t_2), .sel(out_17[2:0]));
  Multiplexer #(.select(3), .width(32)) multiplexer_6 (
    .in0(register_28_q), .in1(register_29_q), .in2(register_30_q), .in3(register_31_q), .in4(register_32_q),
    .in5(register_33_q), .in6(register_34_q), .in7(register_35_q), .out(t_7), .sel(undriven_15));
  buf buffer_5 (buffer_5_out, buffer_4_out);
  buf buffer_6 (buffer_6_out, buffer_5_out);
  T_Flip_Flop t_ff_22 (.T(1'b1), .clk(t_ff_21_qn), .Q(t_ff_21_q[1]), .Qn(t_ff_22_qn));  // open: reset, preset
  assign sigma_1 = xor_7_out ^ {undriven_12[24:0], undriven_12[31:25]};  // XOR_Gate xor_8, 32 bits wide
  T_Flip_Flop t_ff_23 (.T(1'b1), .clk(t_ff_22_qn), .Q(t_ff_21_q[2]), .Qn(t_ff_23_qn));  // open: reset, preset
  Multiplexer #(.select(3), .width(32)) multiplexer_7 (
    .in0(register_28_q), .in1(register_29_q), .in2(register_30_q), .in3(register_31_q), .in4(register_32_q),
    .in5(register_33_q), .in6(register_34_q), .in7(register_35_q), .out(t_15), .sel(undriven_16));
  T_Flip_Flop t_ff_24 (.T(1'b1), .clk(t_ff_23_qn), .Q(t_ff_21_q[3]), .Qn(t_ff_24_qn));  // open: reset, preset
  Multiplexer #(.select(3), .width(32)) multiplexer_8 (
    .in0(register_28_q), .in1(register_29_q), .in2(register_30_q), .in3(register_31_q), .in4(register_32_q),
    .in5(register_33_q), .in6(register_34_q), .in7(register_35_q), .out(t_16), .sel(undriven_23));
  T_Flip_Flop t_ff_25 (.T(1'b1), .clk(t_ff_24_qn), .Q(t_ff_21_q[4]), .Qn(t_ff_25_qn));  // open: reset, preset
  Multiplexer #(.select(3), .width(32)) multiplexer_9 (
    .in0(register_36_q), .in1(register_37_q), .in2(register_38_q), .in3(register_39_q), .in4(register_40_q),
    .in5(register_41_q), .in6(register_42_q), .in7(register_43_q), .out(multiplexer_9_out), .sel(out_17[2:0]));
  Register #(.width(32)) register_44 (.D(undriven_17), .clk(buffer_4_out), .Q(register_44_q));  // open: en, clr
  Register #(.width(32)) register_45 (.D(undriven_10), .clk(buffer_4_out), .Q(register_45_q));  // open: en, clr
  Register #(.width(32)) register_46 (.D(undriven_10), .clk(buffer_4_out), .Q(register_46_q));  // open: en, clr
  Register #(.width(32)) register_47 (.D(undriven_10), .clk(buffer_4_out), .Q(register_47_q));  // open: en, clr
  Register #(.width(32)) register_48 (.D(undriven_10), .clk(buffer_4_out), .Q(register_48_q));  // open: en, clr
  Register #(.width(32)) register_49 (.D(undriven_10), .clk(buffer_4_out), .Q(register_49_q));  // open: en, clr
  Register #(.width(32)) register_50 (.D(undriven_10), .clk(buffer_4_out), .Q(register_50_q));  // open: en, clr
  Register #(.width(32)) register_51 (.D(bit_extender_3_out), .clk(buffer_4_out), .Q(register_51_q));  // open: en, clr
  T_Flip_Flop t_ff_26 (.T(1'b1), .clk(t_ff_25_qn), .Q(t_ff_21_q[5]), .Qn(t_ff_26_qn));  // open: reset, preset
  Multiplexer #(.select(3), .width(32)) multiplexer_10 (
    .in0(register_36_q), .in1(register_37_q), .in2(register_38_q), .in3(register_39_q), .in4(register_40_q),
    .in5(register_41_q), .in6(register_42_q), .in7(register_43_q), .sel(out_19[2:0]));  // open: out
  Multiplexer #(.select(3), .width(32)) multiplexer_11 (
    .in0(register_36_q), .in1(register_37_q), .in2(register_38_q), .in3(register_39_q), .in4(register_40_q),
    .in5(register_41_q), .in6(register_42_q), .in7(register_43_q), .sel(out_24[2:0]));  // open: out
  Multiplexer #(.select(3), .width(32)) multiplexer_12 (
    .in0(register_36_q), .in1(register_37_q), .in2(register_38_q), .in3(register_39_q), .in4(register_40_q),
    .in5(register_41_q), .in6(register_42_q), .in7(register_43_q), .sel(out_28[2:0]));  // open: out
  Register #(.width(32)) register_52 (.D(undriven_18), .clk(undriven_30), .Q(register_52_q));  // open: en, clr
  Register #(.width(32)) register_53 (.D(undriven_19), .clk(undriven_30), .Q(register_53_q));  // open: en, clr
  Register #(.width(32)) register_54 (.clk(undriven_30), .Q(register_54_q));  // open: D, en, clr
  Register #(.width(32)) register_55 (.clk(undriven_30), .Q(register_55_q));  // open: D, en, clr
  Register #(.width(32)) register_56 (.D(undriven_22), .clk(undriven_30), .Q(register_56_q));  // open: en, clr
  Register #(.width(32)) register_57 (.D(undriven_21), .clk(undriven_30), .Q(register_57_q));  // open: en, clr
  Multiplexer #(.select(3), .width(32)) multiplexer_13 (
    .in0(register_44_q), .in1(register_45_q), .in2(register_46_q), .in3(register_47_q), .in4(register_48_q),
    .in5(register_49_q), .in6(register_50_q), .in7(register_51_q), .out(multiplexer_13_out), .sel(out_17[2:0]));
  assign bit_extender_4_out = {{4{1'b0}}, 2'b10};  // Bit_Extender bit_extender_4
  assign bit_extender_5_out = {{3{1'b0}}, 3'b111};  // Bit_Extender bit_extender_5
  assign bit_extender_6_out = {{2{1'b0}}, 4'b1111};  // Bit_Extender bit_extender_6
  assign bit_extender_7_out = {{1{1'b0}}, 5'b10000};  // Bit_Extender bit_extender_7
  Register #(.width(32)) register_58 (.D(undriven_20), .clk(undriven_30), .Q(register_58_q));  // open: en, clr
  Register #(.width(32)) register_59 (.D(undriven_20), .clk(undriven_30), .Q(register_59_q));  // open: en, clr
  Multiplexer #(.select(3), .width(32)) multiplexer_14 (
    .in0(register_44_q), .in1(register_45_q), .in2(register_46_q), .in3(register_47_q), .in4(register_48_q),
    .in5(register_49_q), .in6(register_50_q), .in7(register_51_q), .out(multiplexer_14_out), .sel(undriven_15));
  Subtractor #(.width(6)) subtractor_1 (
    .a(t_ff_21_q), .b(bit_extender_4_out), .out(out_18), .bout(subtractor_1_bout[5]));  // open: bin
  Subtractor #(.width(6)) subtractor_2 (
    .a(t_ff_21_q), .b(bit_extender_5_out), .out(out_20), .bout(subtractor_2_bout[5]));  // open: bin
  Multiplexer #(.select(3), .width(32)) multiplexer_15 (
    .in0(register_44_q), .in1(register_45_q), .in2(register_46_q), .in3(register_47_q), .in4(register_48_q),
    .in5(register_49_q), .in6(register_50_q), .in7(register_51_q), .out(multiplexer_15_out), .sel(undriven_16));
  assign not_3_out = ~{6{subtractor_1_bout[5]}};  // NOT_Gate not_3, 6 bits wide
  assign not_4_out = ~{6{subtractor_2_bout[5]}};  // NOT_Gate not_4, 6 bits wide
  Subtractor #(.width(6)) subtractor_3 (
    .a(t_ff_21_q), .b(bit_extender_6_out), .out(out_25), .bout(subtractor_3_bout[5]));  // open: bin
  Subtractor #(.width(6)) subtractor_4 (
    .a(t_ff_21_q), .b(bit_extender_7_out), .out(out_29), .bout(subtractor_4_bout[5]));  // open: bin
  Multiplexer #(.select(3), .width(32)) multiplexer_16 (
    .in0(register_44_q), .in1(register_45_q), .in2(register_46_q), .in3(register_47_q), .in4(register_48_q),
    .in5(register_49_q), .in6(register_50_q), .in7(register_51_q), .out(multiplexer_16_out), .sel(undriven_23));
  assign out_17 = out_18 & not_3_out;  // AND_Gate and_5, 6 bits wide
  assign out_19 = out_20 & not_4_out;  // AND_Gate and_6, 6 bits wide
  assign not_5_out = ~{6{subtractor_3_bout[5]}};  // NOT_Gate not_5, 6 bits wide
  assign not_6_out = ~{6{subtractor_4_bout[5]}};  // NOT_Gate not_6, 6 bits wide
  Multiplexer #(.select(3), .width(32)) multiplexer_17 (
    .in0(register_52_q), .in1(register_53_q), .in2(register_54_q), .in3(register_55_q), .in4(register_56_q),
    .in5(register_57_q), .in6(register_58_q), .in7(register_59_q), .out(out_33), .sel(out_17[2:0]));
  Register #(.width(32)) register_60 (.D(undriven_24), .clk(undriven_33), .Q(register_60_q));  // open: en, clr
  Register #(.width(32)) register_61 (.D(undriven_25), .clk(undriven_33), .Q(register_61_q));  // open: en, clr
  Register #(.width(32)) register_62 (.clk(undriven_33), .Q(register_62_q));  // open: D, en, clr
  Register #(.width(32)) register_63 (.clk(undriven_33), .Q(register_63_q));  // open: D, en, clr
  Register #(.width(32)) register_64 (.D(undriven_28), .clk(undriven_33), .Q(register_64_q));  // open: en, clr
  Register #(.width(32)) register_65 (.D(undriven_27), .clk(undriven_33), .Q(register_65_q));  // open: en, clr
  Register #(.width(32)) register_66 (.D(undriven_26), .clk(undriven_33), .Q(register_66_q));  // open: en, clr
  Register #(.width(32)) register_67 (.D(undriven_26), .clk(undriven_33), .Q(register_67_q));  // open: en, clr
  assign out_24 = out_25 & not_5_out;  // AND_Gate and_7, 6 bits wide
  assign out_28 = out_29 & not_6_out;  // AND_Gate and_8, 6 bits wide
  Multiplexer #(.select(3), .width(32)) multiplexer_18 (
    .in0(register_52_q), .in1(register_53_q), .in2(register_54_q), .in3(register_55_q), .in4(register_56_q),
    .in5(register_57_q), .in6(register_58_q), .in7(register_59_q), .out(out_35), .sel(out_19[2:0]));
  Multiplexer #(.select(3), .width(32)) multiplexer_19 (
    .in0(register_52_q), .in1(register_53_q), .in2(register_54_q), .in3(register_55_q), .in4(register_56_q),
    .in5(register_57_q), .in6(register_58_q), .in7(register_59_q), .out(out_37), .sel(out_24[2:0]));
  Multiplexer #(.select(3), .width(32)) multiplexer_20 (
    .in0(register_52_q), .in1(register_53_q), .in2(register_54_q), .in3(register_55_q), .in4(register_56_q),
    .in5(register_57_q), .in6(register_58_q), .in7(register_59_q), .out(out_40), .sel(out_28[2:0]));
  Register #(.width(32)) register_68 (.D(undriven_31), .clk(undriven_30), .Q(register_68_q));  // open: en, clr
  Register #(.width(32)) register_69 (.D(undriven_22), .clk(undriven_30), .Q(register_69_q));  // open: en, clr
  Multiplexer #(.select(3), .width(32)) multiplexer_21 (
    .in0(register_60_q), .in1(register_61_q), .in2(register_62_q), .in3(register_63_q), .in4(register_64_q),
    .in5(register_65_q), .in6(register_66_q), .in7(register_67_q), .out(out_9), .sel(out_17[2:0]));
  Register #(.width(32)) register_70 (.D(undriven_22), .clk(undriven_30), .Q(register_70_q));  // open: en, clr
  Register #(.width(32)) register_71 (.D(undriven_22), .clk(undriven_30), .Q(register_71_q));  // open: en, clr
  Register #(.width(32)) register_72 (.D(undriven_22), .clk(undriven_30), .Q(register_72_q));  // open: en, clr
  Register #(.width(32)) register_73 (.D(undriven_22), .clk(undriven_30), .Q(register_73_q));  // open: en, clr
  Register #(.width(32)) register_74 (.D(undriven_22), .clk(undriven_30), .Q(register_74_q));  // open: en, clr
  Register #(.width(32)) register_75 (.D(undriven_29), .clk(undriven_30), .Q(register_75_q));  // open: en, clr
  Multiplexer #(.select(3), .width(32)) multiplexer_22 (
    .in0(register_60_q), .in1(register_61_q), .in2(register_62_q), .in3(register_63_q), .in4(register_64_q),
    .in5(register_65_q), .in6(register_66_q), .in7(register_67_q), .out(out_10), .sel(out_19[2:0]));
  Multiplexer #(.select(3), .width(32)) multiplexer_23 (
    .in0(register_60_q), .in1(register_61_q), .in2(register_62_q), .in3(register_63_q), .in4(register_64_q),
    .in5(register_65_q), .in6(register_66_q), .in7(register_67_q), .out(out_13), .sel(out_24[2:0]));
  Multiplexer #(.select(3), .width(32)) multiplexer_24 (
    .in0(register_60_q), .in1(register_61_q), .in2(register_62_q), .in3(register_63_q), .in4(register_64_q),
    .in5(register_65_q), .in6(register_66_q), .in7(register_67_q), .out(out_15), .sel(out_28[2:0]));
  Multiplexer #(.select(3), .width(32)) multiplexer_25 (
    .in0(register_68_q), .in1(register_69_q), .in2(register_70_q), .in3(register_71_q), .in4(register_72_q),
    .in5(register_73_q), .in6(register_74_q), .in7(register_75_q), .out(multiplexer_25_out), .sel(out_17[2:0]));
  Register #(.width(32)) register_76 (.D(undriven_34), .clk(undriven_33), .Q(register_76_q));  // open: en, clr
  Register #(.width(32)) register_77 (.D(undriven_28), .clk(undriven_33), .Q(register_77_q));  // open: en, clr
  Register #(.width(32)) register_78 (.D(undriven_28), .clk(undriven_33), .Q(register_78_q));  // open: en, clr
  Register #(.width(32)) register_79 (.D(undriven_28), .clk(undriven_33), .Q(register_79_q));  // open: en, clr
  Register #(.width(32)) register_80 (.D(undriven_28), .clk(undriven_33), .Q(register_80_q));  // open: en, clr
  Register #(.width(32)) register_81 (.D(undriven_28), .clk(undriven_33), .Q(register_81_q));  // open: en, clr
  Multiplexer #(.select(3), .width(32)) multiplexer_26 (
    .in0(register_68_q), .in1(register_69_q), .in2(register_70_q), .in3(register_71_q), .in4(register_72_q),
    .in5(register_73_q), .in6(register_74_q), .in7(register_75_q), .sel(out_19[2:0]));  // open: out
  Register #(.width(32)) register_82 (.D(undriven_28), .clk(undriven_33), .Q(register_82_q));  // open: en, clr
  Register #(.width(32)) register_83 (.D(undriven_32), .clk(undriven_33), .Q(register_83_q));  // open: en, clr
  Multiplexer #(.select(3), .width(32)) multiplexer_27 (
    .in0(register_68_q), .in1(register_69_q), .in2(register_70_q), .in3(register_71_q), .in4(register_72_q),
    .in5(register_73_q), .in6(register_74_q), .in7(register_75_q), .sel(out_24[2:0]));  // open: out
  Multiplexer #(.select(3), .width(32)) multiplexer_28 (
    .in0(register_68_q), .in1(register_69_q), .in2(register_70_q), .in3(register_71_q), .in4(register_72_q),
    .in5(register_73_q), .in6(register_74_q), .in7(register_75_q), .sel(out_28[2:0]));  // open: out
  Multiplexer #(.select(3), .width(32)) multiplexer_29 (
    .in0(register_76_q), .in1(register_77_q), .in2(register_78_q), .in3(register_79_q), .in4(register_80_q),
    .in5(register_81_q), .in6(register_82_q), .in7(register_83_q), .out(multiplexer_29_out), .sel(out_17[2:0]));
  Multiplexer #(.select(3), .width(32)) multiplexer_30 (
    .in0(register_76_q), .in1(register_77_q), .in2(register_78_q), .in3(register_79_q), .in4(register_80_q),
    .in5(register_81_q), .in6(register_82_q), .in7(register_83_q), .out(multiplexer_30_out), .sel(out_19[2:0]));
  Multiplexer #(.select(3), .width(32)) multiplexer_31 (
    .in0(register_76_q), .in1(register_77_q), .in2(register_78_q), .in3(register_79_q), .in4(register_80_q),
    .in5(register_81_q), .in6(register_82_q), .in7(register_83_q), .out(multiplexer_31_out), .sel(out_24[2:0]));
  Multiplexer #(.select(3), .width(32)) multiplexer_32 (
    .in0(register_76_q), .in1(register_77_q), .in2(register_78_q), .in3(register_79_q), .in4(register_80_q),
    .in5(register_81_q), .in6(register_82_q), .in7(register_83_q), .out(multiplexer_32_out), .sel(out_28[2:0]));
  Multiplexer #(.select(3), .width(32)) multiplexer_33 (
    .in0(t_2), .in1(multiplexer_13_out), .in2(out_9), .in3(multiplexer_29_out), .in4(out_32),
    .in5(multiplexer_9_out), .in6(out_33), .in7(multiplexer_25_out));  // open: out, sel
  Multiplexer #(.select(3), .width(32)) multiplexer_34 (
    .in0(t_7), .in1(multiplexer_14_out), .in2(out_10), .in3(multiplexer_30_out));  // open: in4, in5, in6, in7, out, sel
  Multiplexer #(.select(3), .width(32)) multiplexer_35 (
    .in0(t_15), .in1(multiplexer_15_out), .in2(out_13), .in3(multiplexer_31_out));  // open: in4, in5, in6, in7, out, sel
  Multiplexer #(.select(3), .width(32)) multiplexer_36 (
    .in0(t_16), .in1(multiplexer_16_out), .in2(out_15), .in3(multiplexer_32_out));  // open: in4, in5, in6, in7, out, sel

  assign right_3 = {3'b000, w_15[31:3]};
  assign rotate_7 = {w_15[6:0], w_15[31:7]};
  assign rotate_18 = {w_15[17:0], w_15[31:18]};

  // Notes on the sheet:
  //   contents of h_values (hex, n*v repeats v):
  //   6a09e667 bb67ae85 3c6ef372 a54ff53a 510e527f 9b05688c 1f83d9ab 5be0cd19
  //   contents of k_values (hex, n*v repeats v):
  //   428a2f98 71374491 b5c0fbcf e9b5dba5 3956c25b 59f111f1 923f82a4 ab1c5ed5 d807aa98 12835b01 234185be
  //   550c7dc3 72be5d74 80deb1fe 9dbc06a7 c19bf174 e49b69c1 efbe4786 fc19dc6 240ca1cc 2de92c6f 4a7484aa
  //   5cb0a9dc 74f988da 983e5152 a831c66d b00327c8 bf597fc7 c6e00bf3 d5a79147 6ca6351 14292967 27b70a85
  //   2e1b2138 4d2c6dfc 53380d13 650a7354 766a0abb 81c2c92e 92722c85 a2bfe8a1 a81a664b c24b8b70 c76c51a3
  //   d192e819 d6990624 f40e3585 106aa070 19a4c116 1e376c08 2748774c 34b0bcb5 391c0cb3 4ed8aa4a 5b9cca4f
  //   682e6ff3 748f82ee 78a5636f 84c87814 8cc70208 90befffa a4506ceb bef9a3f7 c67178f2
endmodule
